# Fritzing sketch phase one (saved by Fritzing 0.9.2b)
breadboards: 1

parts:
  U1 = NodeMCU V1.0
  U3 = RELAY [package=relay-jzc]
  Q1 = TRANSISTOR_NPN [package=to-92-ammo]
  LED1 = LED - 3mm [color="Red (633nm)" package="3 mm [THT]"]
  VCC1 = Battery block 9V

nets:
  N1: U1.GND, Q1.E
  N2: U1.D7, Q1.B
  N3: U1.RSV#40, U3.NO
  N4: U3.COIL2, Q1.C
  N5: U3.NC, VCC1.-
  N6: U3.MAIN, LED1.cathode
  N7: LED1.anode, VCC1.+

custom parts:
  NodeMCU V1.0: ESP8266 based NodeMCU
